# Fritzing sketch freedeck 3x2 (saved by Fritzing 0.9.4)
circuit board: 10.8057cm x 5.96594cm
breadboards: 1

parts:
  Pro_Micro1 = SparkFun Pro Micro
  S4 = SWITCH-MOMENTARY-2 [package=tactile-switch-1101ne]
  S5 = SWITCH-MOMENTARY-2 [package=tactile-switch-1101ne]
  S6 = SWITCH-MOMENTARY-2 [package=tactile-switch-1101ne]
  S1 = SWITCH-MOMENTARY-2 [package=tactile-switch-1101ne]
  S2 = SWITCH-MOMENTARY-2 [package=tactile-switch-1101ne]
  S3 = SWITCH-MOMENTARY-2 [package=tactile-switch-1101ne]
  U1 = 74HC4051 [package=so16]
  U2 = 74HC4051 [package=so16]
  OLED3 = OLED 128x64 I2C Monochrome Display
  OLED2 = OLED 128x64 I2C Monochrome Display
  OLED1 = OLED 128x64 I2C Monochrome Display
  OLED4 = OLED 128x64 I2C Monochrome Display
  OLED5 = OLED 128x64 I2C Monochrome Display
  OLED6 = OLED 128x64 I2C Monochrome Display
  SD_Reader = SD Card SPI Reader

nets:
  N1: Pro_Micro1.TX0, OLED3.SCK, OLED2.SCK, OLED1.SCK, OLED4.SCK, OLED5.SCK, OLED6.SCK
  N2: Pro_Micro1.RX1, U1.IO
  GND: Pro_Micro1.GND, S5.1, S6.1, S1.1, S2.1, S3.1, U1.INH, U1.VSS, U2.INH, U2.VSS, OLED3.GND, OLED2.GND, OLED1.GND, OLED5.GND, OLED6.GND, SD_Reader.GND
  N3: Pro_Micro1.6, U2.IO
  N4: Pro_Micro1.7, U1.A, U2.A
  N5: Pro_Micro1.8, U1.B, U2.B
  N6: Pro_Micro1.9, U1.C, U2.C
  N7: Pro_Micro1.10, SD_Reader.CS_-_Chip_Select
  N8: Pro_Micro1.16, SD_Reader.SI_-_Data_In
  N9: Pro_Micro1.14, SD_Reader.SO_-_Data_Out
  N10: Pro_Micro1.15, SD_Reader.SCK_-_SPI_Clock
  VDD: Pro_Micro1.VCC, U1.VDD, U2.VDD, SD_Reader.+V
  N11: S4.1, OLED4.GND
  N12: S4.2, U2.IO3
  N13: S5.2, U2.IO4
  N14: S6.2, U2.IO5
  N15: S1.2, U2.IO0
  N16: S2.2, U2.IO1
  N17: S3.2, U2.IO2
  N18: U1.IO4, OLED5.SDA
  N19: U1.IO5, OLED6.SDA
  N20: U1.IO3, OLED4.SDA
  N21: U1.IO0, OLED1.SDA
  N22: U1.IO1, OLED2.SDA
  N23: U1.IO2, OLED3.SDA
  VDD_2: OLED3.VDD, OLED6.VDD
  VDD_3: OLED2.VDD, OLED5.VDD
  VDD_4: OLED1.VDD, OLED4.VDD

custom parts:
  SparkFun Pro Micro: The Pro Micro is similar to the Pro Mini except with an ATmega32U4 on board. The USB transceiver inside the 32U4 allows us to add USB connectivity on-board and do away with bulky external USB interface. Based on: https://github.com/unorthodox-engineers/unorthodox-arduino/blob/master/Unorthodox/fritzing/parts/Pro%20Micro.fzpz
  SWITCH-MOMENTARY-2: Various NO switches- pushbuttons, reed, etc
